# Fritzing sketch GPS (saved by Fritzing 0.9.3b)

parts:
  U1 = NodeMCU V3.0
  Part1 = u-blox NEO-6M GPS Breakout

nets:
  N1: U1.D1, Part1.RXD
  N2: U1.D2, Part1.TXD
  GND: U1.GND, Part1.GND
  3V3: U1.3V3, Part1.VCC

custom parts:
  NodeMCU V3.0: ESP8266 based NodeMCU
